// Logisim project Lab3.circ as structural Verilog: 22 circuits, main circuit main
module main (
);

  wire clock_1_out, cpu_1_halt, frontpanelcontroller_1_cpuclk, frontpanelcontroller_1_runhalt, Reset_out,
       RunStop_out, Step_out;
  wire [3:0] cpu_1_alufalgs, cpu_1_flags;
  wire [15:0] cpu_1_alua, cpu_1_alub, cpu_1_dmaddress, cpu_1_dmdata, cpu_1_imaddress, cpu_1_imdata,
       cpu_1_result, cpu_1_writeback, IM_data;

  Clock clock_1 (.out(clock_1_out));
  ROM #(.addrWidth(16), .dataWidth(16)) IM (.addr(cpu_1_imaddress), .data(IM_data));
  FrontPanelController frontpanelcontroller_1 (
    .Clk(clock_1_out), .Run(RunStop_out), .Step(Step_out), .Reset(Reset_out), .Halt(cpu_1_halt),
    .CpuClk(frontpanelcontroller_1_cpuclk), .RunHalt(frontpanelcontroller_1_runhalt));
  CPU cpu_1 (
    .IMDataIn(IM_data), .CLK(frontpanelcontroller_1_cpuclk), .Reset(Reset_out), .Halt(cpu_1_halt),
    .IMAddress(cpu_1_imaddress), .IMdata(cpu_1_imdata), .DMAddress(cpu_1_dmaddress), .DMData(cpu_1_dmdata),
    .WriteBack(cpu_1_writeback), .Flags(cpu_1_flags), .AluA(cpu_1_alua), .AluB(cpu_1_alub),
    .Result(cpu_1_result), .ALUFalgs(cpu_1_alufalgs));
  LED led_1 (.in(cpu_1_flags[3]));
  LED led_2 (.in(cpu_1_flags[2]));
  LED led_3 (.in(cpu_1_flags[1]));
  LED led_4 (.in(cpu_1_flags[0]));
  Hex_Digit_Display hex_digit_display_1 (.value(cpu_1_alua[15:12]));  // open: dp
  LED led_5 (.in(cpu_1_halt));
  Hex_Digit_Display hex_digit_display_2 (.value(cpu_1_imaddress[15:12]));  // open: dp
  Hex_Digit_Display hex_digit_display_3 (.value(cpu_1_imaddress[11:8]));  // open: dp
  Hex_Digit_Display hex_digit_display_4 (.value(cpu_1_imdata[15:12]));  // open: dp
  Hex_Digit_Display hex_digit_display_5 (.value(cpu_1_imdata[11:8]));  // open: dp
  Hex_Digit_Display hex_digit_display_6 (.value(cpu_1_alua[11:8]));  // open: dp
  Hex_Digit_Display hex_digit_display_7 (.value(cpu_1_alua[7:4]));  // open: dp
  LED N (.in(cpu_1_alufalgs[3]));
  LED Z (.in(cpu_1_alufalgs[2]));
  LED C (.in(cpu_1_alufalgs[1]));
  LED led_6 (.in(frontpanelcontroller_1_runhalt));
  Button RunStop (.out(RunStop_out));
  Hex_Digit_Display hex_digit_display_8 (.value(cpu_1_imaddress[7:4]));  // open: dp
  Hex_Digit_Display hex_digit_display_9 (.value(cpu_1_imaddress[3:0]));  // open: dp
  Hex_Digit_Display hex_digit_display_10 (.value(cpu_1_imdata[7:4]));  // open: dp
  // Hex_Digit_Display hex_digit_display_11: pin names not known; wires that end beside it: cpu_1_imdata[3:0]
  Hex_Digit_Display hex_digit_display_12 (.value(cpu_1_alua[3:0]));  // open: dp
  LED V (.in(cpu_1_alufalgs[0]));
  Button Step (.out(Step_out));
  Hex_Digit_Display hex_digit_display_13 (.value(cpu_1_dmaddress[15:12]));  // open: dp
  Hex_Digit_Display hex_digit_display_14 (.value(cpu_1_dmdata[15:12]));  // open: dp
  Hex_Digit_Display hex_digit_display_15 (.value(cpu_1_writeback[15:12]));  // open: dp
  Hex_Digit_Display hex_digit_display_16 (.value(cpu_1_alub[15:12]));  // open: dp
  Hex_Digit_Display hex_digit_display_17 (.value(cpu_1_result[15:12]));  // open: dp
  Button Reset (.out(Reset_out));
  Hex_Digit_Display hex_digit_display_18 (.value(cpu_1_dmaddress[11:8]));  // open: dp
  Hex_Digit_Display hex_digit_display_19 (.value(cpu_1_dmaddress[7:4]));  // open: dp
  Hex_Digit_Display hex_digit_display_20 (.value(cpu_1_dmdata[11:8]));  // open: dp
  Hex_Digit_Display hex_digit_display_21 (.value(cpu_1_dmdata[7:4]));  // open: dp
  Hex_Digit_Display hex_digit_display_22 (.value(cpu_1_writeback[11:8]));  // open: dp
  Hex_Digit_Display hex_digit_display_23 (.value(cpu_1_writeback[7:4]));  // open: dp
  Hex_Digit_Display hex_digit_display_24 (.value(cpu_1_alub[11:8]));  // open: dp
  Hex_Digit_Display hex_digit_display_25 (.value(cpu_1_alub[7:4]));  // open: dp
  Hex_Digit_Display hex_digit_display_26 (.value(cpu_1_result[11:8]));  // open: dp
  Hex_Digit_Display hex_digit_display_27 (.value(cpu_1_result[7:4]));  // open: dp
  Hex_Digit_Display hex_digit_display_28 (.value(cpu_1_dmaddress[3:0]));  // open: dp
  Hex_Digit_Display hex_digit_display_29 (.value(cpu_1_dmdata[3:0]));  // open: dp
  Hex_Digit_Display hex_digit_display_30 (.value(cpu_1_writeback[3:0]));  // open: dp
  Hex_Digit_Display hex_digit_display_31 (.value(cpu_1_alub[3:0]));  // open: dp
  Hex_Digit_Display hex_digit_display_32 (.value(cpu_1_result[3:0]));  // open: dp

  // Notes on the sheet:
  //   N Z C V
  //   Latched Flags
  //   HALT
  //   Instruction Memory
  //   mARMi
  //   ALU A Input
  //   ALU Flags
  //   Data Memory
  //   WriteBack
  //   ALU B Input
  //   ALU Result
endmodule

module CPU (
  input  [15:0] IMDataIn,
  input  CLK,
  input  Reset,
  output Halt,
  output [15:0] IMAddress,
  output [15:0] IMdata,
  output [15:0] DMAddress,
  output [15:0] DMData,
  output [15:0] WriteBack,
  output [3:0] Flags,
  output [15:0] AluA,
  output [15:0] AluB,
  output [15:0] Result,
  output [3:0] ALUFalgs
);

  wire ALUFlag, BEQ, Bimm, BNE, controlled_buffer_1_out, controlled_buffer_2_out, controlled_buffer_3_out,
       JMP, LDR, MOV_flag, MOV_Rd, multiplexer_1_out, multiplexer_2_out, NOP, not_1_out, not_2_out,
       not_3_out, not_4_out, or_2_out, or_3_out, or_4_out, or_5_out, STR, WE3;
  wire [2:0] A1, A2, A3, controlled_buffer_4_out;
  wire [3:0] ALUop, Non_ALU_func;
  wire [15:0] DMDataOut, Flags_mov, multiplexer_4_out, Offset, PCplus1, RD1, RD2;

  Decoder #(.select(3)) decoder_1 (
    .out1(ALUFlag), .sel(IMDataIn[15:13]));  // open: out0, out2, out3, out4, out5, out6, out7, en
  not not_1 (not_1_out, Halt);
  Multiplexer multiplexer_1 (.in0(BNE), .in1(1'b0), .out(multiplexer_1_out), .sel(Flags[2]));
  assign controlled_buffer_1_out = not_1_out ? CLK : 1'bz;  // Controlled_Buffer controlled_buffer_1
  Demultiplexer #(.select(3), .width(4)) demultiplexer_1 (
    .out0(Non_ALU_func), .out1(ALUop), .in(IMDataIn[12:9]), .sel(IMDataIn[15:13]));  // open: out2, out3, out4, out5, out6, out7
  Multiplexer multiplexer_2 (.in0(1'b0), .in1(BEQ), .out(multiplexer_2_out), .sel(Flags[2]));
  or or_1 (JMP, Bimm, multiplexer_1_out, multiplexer_2_out);
  Fetch_unit fetch_unit_1 (
    .CLK(controlled_buffer_1_out), .Reset(Reset), .WBbus(DMAddress), .JMP(JMP), .IMaddress(IMAddress),
    .PCplus1(PCplus1));
  Decoder #(.select(4)) decoder_2 (
    .out4(Bimm), .out6(BEQ), .out7(BNE), .sel(IMDataIn[15:12]));  // open: out0, out1, out2, out3, out5, out8, out9, out10, out11, out12, out13, out14, out15, en
  Decoder #(.select(4)) decoder_3 (
    .out0(NOP), .out3(Halt), .out4(MOV_Rd), .out5(MOV_flag), .out8(LDR), .out12(STR), .sel(Non_ALU_func));  // open: out1, out2, out6, out7, out9, out10, out11, out13, out14, out15, en
  not not_2 (not_2_out, Halt);
  assign controlled_buffer_2_out = not_2_out ? CLK : 1'bz;  // Controlled_Buffer controlled_buffer_2
  not not_3 (not_3_out, Halt);
  assign controlled_buffer_3_out = not_3_out ? CLK : 1'bz;  // Controlled_Buffer controlled_buffer_3
  Register_file register_file_1 (
    .R7(PCplus1), .CLK(controlled_buffer_2_out), .WE3(WE3), .A1(A1), .A2(A2), .A3(A3), .Reset(Reset),
    .WD3(WriteBack), .RD1(RD1), .RD2(RD2), .RD3(DMData));
  Data_Memory data_memory_1 (
    .Address(DMAddress), .WE(STR), .CLK(controlled_buffer_3_out), .DMdataIn(DMData), .DMdataOut(DMDataOut));
  Register #(.width(4)) FlagRegister (.D(ALUFalgs), .en(ALUFlag), .clk(CLK), .Q(Flags), .clr(Reset));
  ALU alu_1 (.A(AluA), .B(AluB), .ALUOp(ALUop), .Result(DMAddress), .FlagsNZCV(ALUFalgs));
  Multiplexer #(.width(16)) multiplexer_3 (.in0(RD1), .in1({16{1'b0}}), .out(AluA), .sel(or_2_out));
  assign Offset = {{4{IMDataIn[11]}}, IMDataIn[11:0]};  // Bit_Extender bit_extender_1
  assign Flags_mov = {{12{1'b0}}, Flags};  // Bit_Extender bit_extender_2
  or or_2 (or_2_out, IMDataIn[15], MOV_flag);
  Multiplexer #(.width(16)) multiplexer_4 (.in0(Offset), .in1(Flags_mov), .out(multiplexer_4_out), .sel(MOV_flag));
  Multiplexer #(.width(16)) multiplexer_5 (.in0(RD2), .in1(multiplexer_4_out), .out(AluB), .sel(or_3_out));
  or or_3 (or_3_out, IMDataIn[15], BEQ, BNE, Bimm, MOV_flag);
  assign controlled_buffer_4_out = not_4_out ? IMDataIn[8:6] : 3'bz;  // Controlled_Buffer controlled_buffer_4
  not not_4 (not_4_out, IMDataIn[15]);
  Multiplexer #(.width(3)) multiplexer_6 (.in0(controlled_buffer_4_out), .in1(3'b111), .out(A1), .sel(or_4_out));
  or or_4 (or_4_out, Bimm, BEQ, BNE);
  assign A2 = not_4_out ? IMDataIn[2:0] : 3'bz;  // Controlled_Buffer controlled_buffer_5
  Multiplexer multiplexer_7 (.in0(1'b1), .in1(1'b0), .out(WE3), .sel(or_5_out));
  or or_5 (or_5_out, Bimm, STR, BEQ, BNE);
  Multiplexer #(.width(3)) multiplexer_8 (.in0(IMDataIn[5:3]), .in1(IMDataIn[14:12]), .out(A3), .sel(IMDataIn[15]));
  Multiplexer #(.width(16)) multiplexer_9 (.in0(DMAddress), .in1(DMDataOut), .out(WriteBack), .sel(LDR));

  assign IMdata = IMDataIn;
  assign Result = DMAddress;

  // Other names for the same wires on the sheet: A[15:0] = AluA; ALUFlags[3:0] = ALUFalgs; B[15:0] = AluB;
  //   IMAdress[15:0] = IMAddress; Branch[3:0] = IMDataIn[15:12]; Opcode[3:0] = IMDataIn[12:9];
  //   Rimm[2:0] = IMDataIn[14:12]; Instr[2:0] = IMDataIn[15:13]; MSB = IMDataIn[15]; Imm[11:0] = IMDataIn[11:0];
  //   Rm[2:0] = IMDataIn[2:0]; Rd[2:0] = IMDataIn[5:3]; Rn[2:0] = IMDataIn[8:6]

  // Notes on the sheet:
  //   Decoding for ALU Flag operation
  //   Branching condition check
  //   check for zero flag
  //   Control for passing OPcode for ALU/Non-ALU
  //   check for zero flag
  //   Decoding for Non-ALU
  //   Decoding for branching
  //   Decoder/Control
  //   Extracting the instructions from memory address
  //   Control for input A to ALU
  //   Control for input B to ALU
  //   Control for register addresses A1, A2, A3 to register file
  //   Control for writing enabled to register file
  //   Writeback to the register file
endmodule

module FrontPanelController (
  input  Clk,
  input  Run,
  input  Step,
  input  Reset,
  input  Halt,
  output CpuClk,
  output RunHalt
);

  wire and_1_out, or_1_out, pull_resistor_1_node, t_ff_1_q;

  T_Flip_Flop t_ff_1 (.T(pull_resistor_1_node), .clk(Run), .Q(t_ff_1_q), .reset(Reset));  // open: Qn, preset
  Pull_Resistor #(.pull(1)) pull_resistor_1 (.node(pull_resistor_1_node));
  or or_1 (or_1_out, t_ff_1_q, Step);
  and and_1 (and_1_out, Clk, t_ff_1_q);
  and and_2 (RunHalt, or_1_out, ~Halt);  // AND_Gate
  Multiplexer multiplexer_1 (.in0(Step), .in1(and_1_out), .out(CpuClk), .sel(t_ff_1_q));
endmodule

module Fetch_unit (
  input  CLK,
  input  Reset,
  input  [15:0] WBbus,
  input  JMP,
  output [15:0] IMaddress,
  output [15:0] PCplus1
);

  wire [15:0] multiplexer_1_out;

  Adder #(.width(16)) adder_1 (.a(IMaddress), .b(16'h1), .out(PCplus1));  // open: cin, cout
  Multiplexer #(.width(16)) multiplexer_1 (.in0(PCplus1), .in1(WBbus), .out(multiplexer_1_out), .sel(JMP));
  Register #(.width(16)) Instruction_fetch (.D(multiplexer_1_out), .en(1'b1), .clk(CLK), .Q(IMaddress), .clr(Reset));

  // Notes on the sheet:
  //   PC + 1
endmodule

module ALU (
  input  [15:0] A,
  input  [15:0] B,
  input  [3:0] ALUOp,
  output [15:0] Result,
  output [3:0] FlagsNZCV
);

  wire [3:0] add_1_negative, and_2c6f6c18_1_negative, asr_1_negative, div_1_negative, eor_1_negative,
       lsl_1_negative, lsr_1_negative, modulus_1_negative, mul_7702e8f9_1_negative, mulu_1_negative,
       not_27d8e4dd_1_negative, or_845c92d5_1_negative, rol_b8758796_1_negative, ror_00d91f97_1_negative,
       sub_1_negative;
  wire [15:0] add_1_result, and_2c6f6c18_1_result, asr_1_result, div_1_result, eor_1_result, lsl_1_result,
       lsr_1_result, modulus_1_result, mul_7702e8f9_1_result, mulu_1_result, not_27d8e4dd_1_result,
       or_845c92d5_1_result, rol_b8758796_1_result, ror_00d91f97_1_result, sub_1_result;

  ADD add_1 (
    .A(A), .B(B), .Result(add_1_result), .Zero(add_1_negative[1]), .Carry(add_1_negative[2]),
    .Negative(add_1_negative[0]), .Overflow(add_1_negative[3]));
  SUB sub_1 (
    .A(A), .B(B), .Result(sub_1_result), .Zero(sub_1_negative[1]), .Carry(sub_1_negative[2]),
    .Negative(sub_1_negative[0]), .Overflow(sub_1_negative[3]));
  MUL_7702e8f9 mul_7702e8f9_1 (
    .A(A), .B(B), .result(mul_7702e8f9_1_result), .Zero(mul_7702e8f9_1_negative[1]),
    .Negative(mul_7702e8f9_1_negative[0]), .Overflow(mul_7702e8f9_1_negative[3]),
    .Carry(mul_7702e8f9_1_negative[2]));
  MULU mulu_1 (
    .A(A), .B(B), .Result(mulu_1_result), .Zero(mulu_1_negative[1]), .Negative(mulu_1_negative[0]),
    .Overflow(mulu_1_negative[3]), .Carry(mulu_1_negative[2]));
  DIV div_1 (
    .A(A), .B(B), .Result(div_1_result), .Zero(div_1_negative[1]), .Negative(div_1_negative[0]),
    .Overflow(div_1_negative[3]), .Carry(div_1_negative[2]));
  Modulus modulus_1 (
    .A(A), .B(B), .Result(modulus_1_result), .zero(modulus_1_negative[1]), .Negative(modulus_1_negative[0]),
    .Overflow(modulus_1_negative[3]), .Carry(modulus_1_negative[2]));
  And_2c6f6c18 and_2c6f6c18_1 (
    .A(A), .B(B), .Result(and_2c6f6c18_1_result), .Zero(and_2c6f6c18_1_negative[1]),
    .Carry(and_2c6f6c18_1_negative[2]), .Overflow(and_2c6f6c18_1_negative[3]),
    .Negative(and_2c6f6c18_1_negative[0]));
  Or_845c92d5 or_845c92d5_1 (
    .A(A), .B(B), .Result(or_845c92d5_1_result), .Zero(or_845c92d5_1_negative[1]),
    .Carry(or_845c92d5_1_negative[2]), .Overflow(or_845c92d5_1_negative[3]),
    .Negative(or_845c92d5_1_negative[0]));
  EOR eor_1 (
    .A(A), .B(B), .Result(eor_1_result), .Zero(eor_1_negative[1]), .Carry(eor_1_negative[2]),
    .Overflow(eor_1_negative[3]), .Negative(eor_1_negative[0]));
  Not_27d8e4dd not_27d8e4dd_1 (
    .A(A), .Result(not_27d8e4dd_1_result), .Zero(not_27d8e4dd_1_negative[1]),
    .Carry(not_27d8e4dd_1_negative[2]), .Overflow(not_27d8e4dd_1_negative[3]),
    .Negative(not_27d8e4dd_1_negative[0]));
  LSL lsl_1 (
    .A(A), .in_2(B), .Result(lsl_1_result), .Zero(lsl_1_negative[1]), .Overflow(lsl_1_negative[3]),
    .Negative(lsl_1_negative[0]), .Carry(lsl_1_negative[2]));
  LSR lsr_1 (
    .A(A), .B(B), .Result(lsr_1_result), .Zero(lsr_1_negative[1]), .Overflow(lsr_1_negative[3]),
    .Negative(lsr_1_negative[0]), .Carry(lsr_1_negative[2]));
  ASR asr_1 (
    .A(A), .B(B), .result(asr_1_result), .Zero(asr_1_negative[1]), .Overflow(asr_1_negative[3]),
    .Negative(asr_1_negative[0]), .Carry(asr_1_negative[2]));
  ROL_b8758796 rol_b8758796_1 (
    .A(A), .B(B), .Result(rol_b8758796_1_result), .Zero(rol_b8758796_1_negative[1]),
    .Overflow(rol_b8758796_1_negative[3]), .Negative(rol_b8758796_1_negative[0]),
    .Carry(rol_b8758796_1_negative[2]));
  ROR_00d91f97 ror_00d91f97_1 (
    .A(A), .B(B), .Result(ror_00d91f97_1_result), .Zero(ror_00d91f97_1_negative[1]),
    .Overflow(ror_00d91f97_1_negative[3]), .Negative(ror_00d91f97_1_negative[0]),
    .Carry(ror_00d91f97_1_negative[2]));
  Multiplexer #(.select(4), .width(16)) multiplexer_1 (
    .in0(add_1_result), .in1(sub_1_result), .in2(mul_7702e8f9_1_result), .in3(mulu_1_result),
    .in4(div_1_result), .in5(modulus_1_result), .in6(and_2c6f6c18_1_result), .in7(or_845c92d5_1_result),
    .in8(eor_1_result), .in9(not_27d8e4dd_1_result), .in10(lsl_1_result), .in11(lsr_1_result),
    .in12(asr_1_result), .in13(rol_b8758796_1_result), .in14(ror_00d91f97_1_result), .out(Result), .sel(ALUOp));  // open: in15
  Multiplexer #(.select(4), .width(4)) multiplexer_2 (
    .in0(add_1_negative), .in1(sub_1_negative), .in2(mul_7702e8f9_1_negative), .in3(mulu_1_negative),
    .in4(div_1_negative), .in5(modulus_1_negative), .in6(and_2c6f6c18_1_negative),
    .in7(or_845c92d5_1_negative), .in8(eor_1_negative), .in9(not_27d8e4dd_1_negative), .in10(lsl_1_negative),
    .in11(lsr_1_negative), .in12(asr_1_negative), .in13(rol_b8758796_1_negative),
    .in14(ror_00d91f97_1_negative), .out({FlagsNZCV[0], FlagsNZCV[1], FlagsNZCV[2], FlagsNZCV[3]}),
    .sel(ALUOp));  // open: in15

  // Notes on the sheet:
  //   Inputs:
  //   A, B - 16 bits
  //   ALUop - 4bits
  //   Outputs:
  //   Flags NZCV
  //   Result
  //   - Negative, zero, carry, overflow
endmodule

module Register_file (
  input  [15:0] R7,
  input  CLK,
  input  WE3,
  input  [2:0] A1,
  input  [2:0] A2,
  input  [2:0] A3,
  input  Reset,
  input  [15:0] WD3,
  output [15:0] RD1,
  output [15:0] RD2,
  output [15:0] RD3
);

  wire demultiplexer_1_out0, demultiplexer_1_out1, demultiplexer_1_out2, demultiplexer_1_out3,
       demultiplexer_1_out4, demultiplexer_1_out5, demultiplexer_1_out6;
  wire [15:0] R0_q, R1_q, R2_q, R3_q, R4_q, R5_q, R6_q;

  Demultiplexer #(.select(3)) demultiplexer_1 (
    .out0(demultiplexer_1_out0), .out1(demultiplexer_1_out1), .out2(demultiplexer_1_out2),
    .out3(demultiplexer_1_out3), .out4(demultiplexer_1_out4), .out5(demultiplexer_1_out5),
    .out6(demultiplexer_1_out6), .in(WE3), .sel(A3));  // open: out7
  Register #(.width(16)) R0 (.D(WD3), .en(demultiplexer_1_out0), .clk(CLK), .Q(R0_q), .clr(Reset));
  Register #(.width(16)) R1 (.D(WD3), .en(demultiplexer_1_out1), .clk(CLK), .Q(R1_q), .clr(Reset));
  Register #(.width(16)) R2 (.D(WD3), .en(demultiplexer_1_out2), .clk(CLK), .Q(R2_q), .clr(Reset));
  Register #(.width(16)) R3 (.D(WD3), .en(demultiplexer_1_out3), .clk(CLK), .Q(R3_q), .clr(Reset));
  Register #(.width(16)) R4 (.D(WD3), .en(demultiplexer_1_out4), .clk(CLK), .Q(R4_q), .clr(Reset));
  Register #(.width(16)) R5 (.D(WD3), .en(demultiplexer_1_out5), .clk(CLK), .Q(R5_q), .clr(Reset));
  Register #(.width(16)) R6 (.D(WD3), .en(demultiplexer_1_out6), .clk(CLK), .Q(R6_q), .clr(Reset));
  Multiplexer #(.select(3), .width(16)) multiplexer_1 (
    .in0(R0_q), .in1(R1_q), .in2(R2_q), .in3(R3_q), .in4(R4_q), .in5(R5_q), .in6(R6_q), .in7(R7), .out(RD1),
    .sel(A1));
  Multiplexer #(.select(3), .width(16)) multiplexer_2 (
    .in0(R0_q), .in1(R1_q), .in2(R2_q), .in3(R3_q), .in4(R4_q), .in5(R5_q), .in6(R6_q), .in7(R7), .out(RD2),
    .sel(A2));
  Multiplexer #(.select(3), .width(16)) multiplexer_3 (
    .in0(R0_q), .in1(R1_q), .in2(R2_q), .in3(R3_q), .in4(R4_q), .in5(R5_q), .in6(R6_q), .in7(R7), .out(RD3),
    .sel(A3));
endmodule

module Data_Memory (
  input  [15:0] Address,
  input  WE,
  input  CLK,
  input  [15:0] DMdataIn,
  output [15:0] DMdataOut
);

  wire comparator_1_gt, not_1_out;
  wire [15:0] controlled_buffer_1_out;

  Comparator #(.width(16)) comparator_1 (.a(Address), .b(16'hf7ff), .gt(comparator_1_gt));  // open: eq, lt
  assign controlled_buffer_1_out = comparator_1_gt ? Address : 16'bz;  // Controlled_Buffer controlled_buffer_1
  not not_1 (not_1_out, WE);
  RAM #(.addrWidth(16), .asyncread("true"), .dataWidth(16)) ram_1 (
    .addr(controlled_buffer_1_out), .we(WE), .oe(not_1_out), .clk(CLK), .din(DMdataIn), .dout(DMdataOut));

  // Notes on the sheet:
  //   Reserve 2k memory
endmodule

module ADD (
  input  [15:0] A,
  input  [15:0] B,
  output [15:0] Result,
  output Zero,
  output Carry,
  output Negative,
  output Overflow
);

  wire bitselector_1_out, bitselector_2_out, bitselector_3_out, not_1_out, xor_1_out, xor_2_out;
  wire [15:0] nor_1_out;

  BitSelector #(.width(16)) bitselector_1 (.in(A), .out(bitselector_1_out), .sel(4'b1111));
  BitSelector #(.width(16)) bitselector_2 (.in(B), .out(bitselector_2_out), .sel(4'b1111));
  Adder #(.width(16)) adder_1 (.a(A), .b(B), .out(Result), .cout(Carry));  // open: cin
  xor xor_1 (xor_1_out, bitselector_1_out, bitselector_2_out);
  not not_1 (not_1_out, xor_1_out);
  BitSelector #(.width(16)) bitselector_3 (.in(Result), .out(bitselector_3_out), .sel(4'b1111));
  xor xor_2 (xor_2_out, not_1_out, bitselector_3_out);
  not not_2 (Overflow, xor_2_out);
  assign nor_1_out = ~(Result | Result);  // NOR_Gate nor_1, 16 bits wide
  BitSelector #(.width(16)) bitselector_4 (.in(Result), .out(Negative), .sel(4'b1111));
  Comparator #(.width(16)) comparator_1 (.a(nor_1_out), .b({16{1'b1}}), .eq(Zero));  // open: gt, lt
endmodule

module SUB (
  input  [15:0] A,
  input  [15:0] B,
  output [15:0] Result,
  output Zero,
  output Carry,
  output Negative,
  output Overflow
);

  wire bitselector_1_out, bitselector_2_out, bitselector_3_out, not_1_out, xor_1_out, xor_2_out;
  wire [15:0] nor_1_out;

  BitSelector #(.width(16)) bitselector_1 (.in(A), .out(bitselector_1_out), .sel(4'b1111));
  BitSelector #(.width(16)) bitselector_2 (.in(B), .out(bitselector_2_out), .sel(4'b1111));
  Subtractor #(.width(16)) subtractor_1 (.a(A), .b(B), .out(Result), .bout(Carry));  // open: bin
  xor xor_1 (xor_1_out, bitselector_1_out, bitselector_2_out);
  not not_1 (not_1_out, xor_1_out);
  BitSelector #(.width(16)) bitselector_3 (.in(Result), .out(bitselector_3_out), .sel(4'b1111));
  xor xor_2 (xor_2_out, not_1_out, bitselector_3_out);
  not not_2 (Overflow, xor_2_out);
  assign nor_1_out = ~(Result | Result);  // NOR_Gate nor_1, 16 bits wide
  BitSelector #(.width(16)) bitselector_4 (.in(Result), .out(Negative), .sel(4'b1111));
  Comparator #(.width(16)) comparator_1 (.a(nor_1_out), .b({16{1'b1}}), .eq(Zero));  // open: gt, lt
endmodule

module MULU (
  input  [15:0] A,
  input  [15:0] B,
  output [15:0] Result,
  output Zero,
  output Negative,
  output Overflow,
  output Carry
);

  wire bitselector_1_out, bitselector_2_out, bitselector_3_out, not_1_out, xor_1_out, xor_2_out;
  wire [15:0] multiplier_1_out, nor_1_out;

  BitSelector #(.width(16)) bitselector_1 (.in(A), .out(bitselector_1_out), .sel(4'b1111));
  BitSelector #(.width(16)) bitselector_2 (.in(B), .out(bitselector_2_out), .sel(4'b1111));
  Multiplier #(.width(16)) multiplier_1 (.a(A), .b(B), .out(multiplier_1_out), .cout(Result));  // open: cin
  xor xor_1 (xor_1_out, bitselector_1_out, bitselector_2_out);
  not not_1 (not_1_out, xor_1_out);
  BitSelector #(.width(16)) bitselector_3 (.in(multiplier_1_out), .out(bitselector_3_out), .sel(4'b1111));
  xor xor_2 (xor_2_out, not_1_out, bitselector_3_out);
  not not_2 (Overflow, xor_2_out);
  assign nor_1_out = ~(multiplier_1_out | multiplier_1_out);  // NOR_Gate nor_1, 16 bits wide
  BitSelector #(.width(16)) bitselector_4 (.in(multiplier_1_out), .out(Negative), .sel(4'b1111));
  Comparator #(.width(16)) comparator_1 (.a(nor_1_out), .b({16{1'b1}}), .eq(Zero));  // open: gt, lt

  assign Carry = 1'b0;
endmodule

module MUL_7702e8f9 (
  input  [15:0] A,
  input  [15:0] B,
  output [15:0] result,
  output Zero,
  output Negative,
  output Overflow,
  output Carry
);

  wire [15:0] nor_1_out;

  Multiplier #(.width(16)) multiplier_1 (.a(A), .b(B), .out(result));  // open: cin, cout
  assign nor_1_out = ~(result | result);  // NOR_Gate nor_1, 16 bits wide
  BitSelector #(.width(16)) bitselector_1 (.in(result), .out(Negative), .sel(4'b1111));
  Comparator #(.width(16)) comparator_1 (.a(nor_1_out), .b({16{1'b1}}), .eq(Zero));  // open: gt, lt

  assign Carry = 1'b0;
  assign Overflow = 1'b0;
endmodule

module DIV (
  input  [15:0] A,
  input  [15:0] B,
  output [15:0] Result,
  output Zero,
  output Negative,
  output Overflow,
  output Carry
);

  wire [15:0] nor_1_out;

  Divider #(.width(16)) divider_1 (.a(A), .b(B), .out(Result));  // open: upper, rem
  assign nor_1_out = ~(Result | Result);  // NOR_Gate nor_1, 16 bits wide
  BitSelector #(.width(16)) bitselector_1 (.in(Result), .out(Negative), .sel(4'b1111));
  Comparator #(.width(16)) comparator_1 (.a(nor_1_out), .b({16{1'b1}}), .eq(Zero));  // open: gt, lt

  assign Carry = 1'b0;
  assign Overflow = 1'b0;
endmodule

module Modulus (
  input  [15:0] A,
  input  [15:0] B,
  output [15:0] Result,
  output zero,
  output Negative,
  output Overflow,
  output Carry
);

  wire [15:0] nor_1_out;

  Divider #(.width(16)) divider_1 (.a(A), .b(B), .rem(Result));  // open: out, upper
  assign nor_1_out = ~(Result | Result);  // NOR_Gate nor_1, 16 bits wide
  BitSelector #(.width(16)) bitselector_1 (.in(Result), .out(Negative), .sel(4'b1111));
  Comparator #(.width(16)) comparator_1 (.a(nor_1_out), .b({16{1'b1}}), .eq(zero));  // open: gt, lt

  assign Carry = 1'b0;
  assign Overflow = 1'b0;
endmodule

module And_2c6f6c18 (
  input  [15:0] A,
  input  [15:0] B,
  output [15:0] Result,
  output Zero,
  output Carry,
  output Overflow,
  output Negative
);

  wire [15:0] nor_1_out;

  assign Result = A & B;  // AND_Gate and_1, 16 bits wide
  assign nor_1_out = ~(Result | Result);  // NOR_Gate nor_1, 16 bits wide
  BitSelector #(.width(16)) bitselector_1 (.in(Result), .out(Negative), .sel(4'b1111));
  Comparator #(.width(16)) comparator_1 (.a(nor_1_out), .b({16{1'b1}}), .eq(Zero));  // open: gt, lt

  assign Carry = 1'b0;
  assign Overflow = 1'b0;
endmodule

module Or_845c92d5 (
  input  [15:0] A,
  input  [15:0] B,
  output [15:0] Result,
  output Zero,
  output Carry,
  output Overflow,
  output Negative
);

  wire [15:0] nor_1_out;

  assign Result = A | B;  // OR_Gate or_1, 16 bits wide
  assign nor_1_out = ~(Result | Result);  // NOR_Gate nor_1, 16 bits wide
  BitSelector #(.width(16)) bitselector_1 (.in(Result), .out(Negative), .sel(4'b1111));
  Comparator #(.width(16)) comparator_1 (.a(nor_1_out), .b({16{1'b1}}), .eq(Zero));  // open: gt, lt

  assign Carry = 1'b0;
  assign Overflow = 1'b0;
endmodule

module EOR (
  input  [15:0] A,
  input  [15:0] B,
  output [15:0] Result,
  output Zero,
  output Carry,
  output Overflow,
  output Negative
);

  wire [15:0] nor_1_out;

  assign Result = A ^ B;  // XOR_Gate xor_1, 16 bits wide
  assign nor_1_out = ~(Result | Result);  // NOR_Gate nor_1, 16 bits wide
  BitSelector #(.width(16)) bitselector_1 (.in(Result), .out(Negative), .sel(4'b1111));
  Comparator #(.width(16)) comparator_1 (.a(nor_1_out), .b({16{1'b1}}), .eq(Zero));  // open: gt, lt

  assign Carry = 1'b0;
  assign Overflow = 1'b0;
endmodule

module Not_27d8e4dd (
  input  [15:0] A,
  output [15:0] Result,
  output Zero,
  output Carry,
  output Overflow,
  output Negative
);

  wire [15:0] nor_1_out;

  assign Result = ~A;  // NOT_Gate not_1, 16 bits wide
  assign nor_1_out = ~(Result | Result);  // NOR_Gate nor_1, 16 bits wide
  BitSelector #(.width(16)) bitselector_1 (.in(Result), .out(Negative), .sel(4'b1111));
  Comparator #(.width(16)) comparator_1 (.a(nor_1_out), .b({16{1'b1}}), .eq(Zero));  // open: gt, lt

  assign Carry = 1'b0;
  assign Overflow = 1'b0;
endmodule

module LSL (
  input  [15:0] A,
  input  [15:0] in_2,
  output [15:0] Result,
  output Zero,
  output Overflow,
  output Negative,
  output Carry
);

  wire [15:0] nor_1_out;

  Shifter #(.width(16)) shifter_1 (.in(A), .\dist (in_2[3:0]), .out(Result));
  assign nor_1_out = ~(Result | Result);  // NOR_Gate nor_1, 16 bits wide
  BitSelector #(.width(16)) bitselector_1 (.in(Result), .out(Negative), .sel(4'b1111));
  Comparator #(.width(16)) comparator_1 (.a(nor_1_out), .b({16{1'b1}}), .eq(Zero));  // open: gt, lt

  assign Carry = 1'b0;
  assign Overflow = 1'b0;
endmodule

module LSR (
  input  [15:0] A,
  input  [15:0] B,
  output [15:0] Result,
  output Zero,
  output Overflow,
  output Negative,
  output Carry
);

  wire [15:0] nor_1_out;

  Shifter #(.shift("lr"), .width(16)) shifter_1 (.in(A), .\dist (B[3:0]), .out(Result));
  BitSelector #(.width(16)) bitselector_1 (.in(Result), .out(Negative), .sel(4'b1111));
  assign nor_1_out = ~(Result | Result);  // NOR_Gate nor_1, 16 bits wide
  Comparator #(.width(16)) comparator_1 (.a(nor_1_out), .b({16{1'b1}}), .eq(Zero));  // open: gt, lt

  assign Carry = 1'b0;
  assign Overflow = 1'b0;
endmodule

module ASR (
  input  [15:0] A,
  input  [15:0] B,
  output [15:0] result,
  output Zero,
  output Overflow,
  output Negative,
  output Carry
);

  wire [15:0] nor_1_out;

  Shifter #(.shift("ar"), .width(16)) shifter_1 (.in(A), .\dist (B[3:0]), .out(result));
  BitSelector #(.width(16)) bitselector_1 (.in(result), .out(Negative), .sel(4'b1111));
  assign nor_1_out = ~(result | result);  // NOR_Gate nor_1, 16 bits wide
  Comparator #(.width(16)) comparator_1 (.a(nor_1_out), .b({16{1'b1}}), .eq(Zero));  // open: gt, lt

  assign Carry = 1'b0;
  assign Overflow = 1'b0;
endmodule

module ROL_b8758796 (
  input  [15:0] A,
  input  [15:0] B,
  output [15:0] Result,
  output Zero,
  output Overflow,
  output Negative,
  output Carry
);

  wire [15:0] nor_1_out;

  Shifter #(.shift("rl"), .width(16)) shifter_1 (.in(A), .\dist (B[3:0]), .out(Result));
  BitSelector #(.width(16)) bitselector_1 (.in(Result), .out(Negative), .sel(4'b1111));
  assign nor_1_out = ~(Result | Result);  // NOR_Gate nor_1, 16 bits wide
  Comparator #(.width(16)) comparator_1 (.a(nor_1_out), .b({16{1'b1}}), .eq(Zero));  // open: gt, lt

  assign Carry = 1'b0;
  assign Overflow = 1'b0;
endmodule

module ROR_00d91f97 (
  input  [15:0] A,
  input  [15:0] B,
  output [15:0] Result,
  output Zero,
  output Overflow,
  output Negative,
  output Carry
);

  wire [15:0] nor_1_out;

  Shifter #(.shift("rr"), .width(16)) shifter_1 (.in(A), .\dist (B[3:0]), .out(Result));
  BitSelector #(.width(16)) bitselector_1 (.in(Result), .out(Negative), .sel(4'b1111));
  assign nor_1_out = ~(Result | Result);  // NOR_Gate nor_1, 16 bits wide
  Comparator #(.width(16)) comparator_1 (.a(nor_1_out), .b({16{1'b1}}), .eq(Zero));  // open: gt, lt

  assign Carry = 1'b0;
  assign Overflow = 1'b0;
endmodule
